// Logisim project 32-np-nc.circ as structural Verilog: 16 circuits, main circuit main
module main (
);

  wire ALU_In_1, ALU_In_2, BComp_U, clk, clk_out, End, Eq, Error, Invalid_Instr, LT, Next_PC_Sel, RAM_Read_U,
       RAM_WEn, Reg_WEn, RESET, Stop_Exec, t_ff_2_qn;
  wire [1:0] WB_Sel;
  wire [2:0] Imm_Enc;
  wire [3:0] ALU_Op;
  wire [23:0] adder_1_out, PC, shifter_1_out;
  wire [31:0] ALU, bit_extender_1_out, bit_extender_2_out, Imm, Instr, multiplexer_1_out, multiplexer_2_out,
       RAM_Out, rs1, rs2, WB_Data;

  PC pc_1 (.clk(clk), .PC_Out(PC), .clear(RESET), .ALU_Out(ALU), .Next_PC_Sel(Next_PC_Sel));
  T_Flip_Flop t_ff_1 (.clk(clk), .T(Invalid_Instr), .Q(Error), .reset(RESET));  // open: Qn, preset, en
  T_Flip_Flop t_ff_2 (.clk(clk), .T(Stop_Exec), .Q(End), .Qn(t_ff_2_qn), .reset(RESET));  // open: preset, en
  Clock u_clk (.out(clk_out));
  Button button_1 (.out(RESET));
  Shifter #(.width(24), .shift("lr")) shifter_1 (.in(PC), .\dist (5'b00010), .out(shifter_1_out));
  and and_1 (clk, t_ff_2_qn, clk_out);
  LED led_1 (.in(End));
  LED led_2 (.in(Error));
  ROM #(.addrWidth(24), .dataWidth(32)) rom_1 (.addr(shifter_1_out), .data(Instr));  // open: sel
  Control control_1 (
    .Instr(Instr), .LT(LT), .Eq(Eq), .Imm_Enc(Imm_Enc), .BComp_U(BComp_U), .ALU_In_1(ALU_In_1),
    .ALU_In_2(ALU_In_2), .ALU_Op(ALU_Op), .RAM_WEn(RAM_WEn), .WB_Sel(WB_Sel), .Reg_WEn(Reg_WEn),
    .Next_PC_Sel(Next_PC_Sel), .RAM_Read_U(RAM_Read_U), .Continue_Execution(Stop_Exec),
    .Valid_Instr(Invalid_Instr));
  Imm_Decoder imm_decoder_1 (.Imm_Bits(Instr[31:7]), .Immediate(Imm), .Imm_Encoding(Imm_Enc));
  Branch_Comp branch_comp_1 (.rs1(rs1), .Unsign(BComp_U), .rs2(rs2), .Eq(Eq), .LT(LT));
  assign bit_extender_1_out = {{8{1'b0}}, PC};  // Bit_Extender bit_extender_1
  Regs regs_1 (
    .Write_Data(WB_Data), .clk(clk), .clr(RESET), .Reg1(Instr[19:15]), .Reg2(Instr[24:20]),
    .Wr_Reg(Instr[11:7]), .wen(Reg_WEn), .Reg1_Data(rs1), .Reg2_Data(rs2));  // open: x0, x1, x2, x3, x4, x5, x6, x7, x16, x17, x18, x19, x20, x21, x22, x23, x8, x9, x10, x11, x12, x13, x14, x15, x24, x25, x26, x27, x28, x29, x30, x31
  Multiplexer #(.width(32), .enable("false")) multiplexer_1 (
    .in0(rs1), .in1(bit_extender_1_out), .out(multiplexer_1_out), .sel(ALU_In_1));
  ALU alu_1 (.In_1(multiplexer_1_out), .In_2(multiplexer_2_out), .Out(ALU), .Op(ALU_Op));
  Multiplexer #(.width(32), .enable("false")) multiplexer_2 (
    .in0(rs2), .in1(Imm), .out(multiplexer_2_out), .sel(ALU_In_2));
  RAM ram_1 (
    .ALU(ALU), .Write_Data(rs2), .clk(clk), .clr(RESET), .Wr_En(RAM_WEn), .Funct3(Instr[14:12]),
    .Read_Unsigned(RAM_Read_U), .RAM_Out(RAM_Out));
  Adder #(.width(24)) adder_1 (.a(24'h4), .b(PC), .out(adder_1_out));  // open: cin, cout
  assign bit_extender_2_out = {{8{1'b0}}, adder_1_out};  // Bit_Extender bit_extender_2
  Multiplexer #(.select(2), .width(32), .enable("false")) multiplexer_3 (
    .in0(bit_extender_2_out), .in1(ALU), .in2(RAM_Out), .in3(32'hbad), .out(WB_Data), .sel(WB_Sel));

  // Notes on the sheet:
  //   Text
  //   contents of rom_1 (hex, n*v repeats v):
  //   140413 e00493 941433 404b3 8482b3 fffff0b7
  //   Execution Control
  //   ALU Control
  //   RAM Control
  //   Regfile Control
endmodule

module PC (
  input  [31:0] ALU_Out,
  input  Next_PC_Sel,
  input  clk,
  input  clear,
  output [23:0] PC_Out
);

  wire [23:0] multiplexer_1_out, PC___4;

  Multiplexer #(.width(24), .enable("false")) multiplexer_1 (
    .in0(PC___4), .in1(ALU_Out[23:0]), .out(multiplexer_1_out), .sel(Next_PC_Sel));
  Register #(.width(24)) PC (.D(multiplexer_1_out), .Q(PC_Out), .clk(clk), .clr(clear));  // open: en
  Adder #(.width(24)) adder_1 (.a(24'h4), .b(PC_Out), .out(PC___4));  // open: cin, cout
endmodule

module Regs (
  input  [31:0] Write_Data,
  input  clk,
  input  clr,
  input  [4:0] Reg1,
  input  [4:0] Reg2,
  input  [4:0] Wr_Reg,
  input  wen,
  output [31:0] x0,
  output [31:0] x1,
  output [31:0] x2,
  output [31:0] x3,
  output [31:0] x4,
  output [31:0] x5,
  output [31:0] x6,
  output [31:0] x7,
  output [31:0] x16,
  output [31:0] x17,
  output [31:0] x18,
  output [31:0] x19,
  output [31:0] x20,
  output [31:0] x21,
  output [31:0] x22,
  output [31:0] x23,
  output [31:0] Reg1_Data,
  output [31:0] Reg2_Data,
  output [31:0] x8,
  output [31:0] x9,
  output [31:0] x10,
  output [31:0] x11,
  output [31:0] x12,
  output [31:0] x13,
  output [31:0] x14,
  output [31:0] x15,
  output [31:0] x24,
  output [31:0] x25,
  output [31:0] x26,
  output [31:0] x27,
  output [31:0] x28,
  output [31:0] x29,
  output [31:0] x30,
  output [31:0] x31
);

  wire wen0, wen1, wen2, wen3;
  wire [31:0] b0_Reg1, b0_Reg2, b1_Reg1, b1_Reg2, b2_Reg1, b2_Reg2, b3_Reg1, b3_Reg2;

  Demultiplexer #(.select(2), .disabled(0), .enable("false")) demultiplexer_1 (
    .out0(wen0), .out1(wen1), .out2(wen2), .out3(wen3), .in(wen), .sel(Wr_Reg[4:3]));
  _8_Reg_w_x0 u_8_reg_w_x0_1 (
    .Write_Data(Write_Data), .clk(clk), .clr(clr), .Wr_Reg__0_2(Wr_Reg[2:0]), .wen(wen0),
    .Reg1_Data(b0_Reg1), .Reg2_Data(b0_Reg2), .Reg1__0_2(Reg1[2:0]), .Reg2__0_2(Reg2[2:0]));
  _8_Reg u_8_reg_1 (
    .Write_Data(Write_Data), .clk(clk), .clr(clr), .Wr_Reg__0_2(Wr_Reg[2:0]), .wen(wen1),
    .Reg1_Data(b1_Reg1), .Reg2_Data(b1_Reg2), .Reg1__0_2(Reg1[2:0]), .Reg2__0_2(Reg2[2:0]));
  _8_Reg u_8_reg_2 (
    .Write_Data(Write_Data), .clk(clk), .clr(clr), .Wr_Reg__0_2(Wr_Reg[2:0]), .wen(wen2),
    .Reg1_Data(b2_Reg1), .Reg2_Data(b2_Reg2), .Reg1__0_2(Reg1[2:0]), .Reg2__0_2(Reg2[2:0]));
  _8_Reg u_8_reg_3 (
    .Write_Data(Write_Data), .clk(clk), .clr(clr), .Wr_Reg__0_2(Wr_Reg[2:0]), .wen(wen3),
    .Reg1_Data(b3_Reg1), .Reg2_Data(b3_Reg2), .Reg1__0_2(Reg1[2:0]), .Reg2__0_2(Reg2[2:0]));
  Multiplexer #(.select(2), .width(32), .enable("false")) multiplexer_1 (
    .in0(b0_Reg1), .in1(b1_Reg1), .in2(b2_Reg1), .in3(b3_Reg1), .out(Reg1_Data), .sel(Reg1[4:3]));
  Multiplexer #(.select(2), .width(32), .enable("false")) multiplexer_2 (
    .in0(b0_Reg2), .in1(b1_Reg2), .in2(b2_Reg2), .in3(b3_Reg2), .out(Reg2_Data), .sel(Reg2[4:3]));

  // Other names for the same wires on the sheet: Reg1__0_2[2:0] = Reg1[2:0]; Reg1__3_4[1:0] = Reg1[4:3];
  //   Reg2__0_2[2:0] = Reg2[2:0]; Reg2__3_4[1:0] = Reg2[4:3]; WD[31:0] = Write_Data; Wr_Reg__0_2[2:0] = Wr_Reg[2:0]

  // Notes on the sheet:
  //   x0-7
  //   b0
  //   x8-15
  //   b1
  //   x16-23
  //   b2
  //   x24-31
  //   b3
endmodule

module _8_Reg_w_x0 (
  input  [31:0] Write_Data,
  input  [2:0] Reg1__0_2,
  input  clk,
  input  clr,
  input  [2:0] Wr_Reg__0_2,
  input  wen,
  input  [2:0] Reg2__0_2,
  output [31:0] Reg1_Data,
  output [31:0] Reg2_Data
);

  wire en1, en2, en3, en4, en5, en6, en7;
  wire [31:0] r1, r2, r3, r4, r5, r6, r7;

  Demultiplexer #(.select(3), .enable("false")) demultiplexer_1 (
    .out1(en1), .out2(en2), .out3(en3), .out4(en4), .out5(en5), .out6(en6), .out7(en7), .in(wen),
    .sel(Wr_Reg__0_2));  // open: out0
  Register #(.width(32)) u_r1 (.D(Write_Data), .en(en1), .Q(r1), .clk(clk), .clr(clr));
  Register #(.width(32)) u_r2 (.D(Write_Data), .en(en2), .Q(r2), .clk(clk), .clr(clr));
  Register #(.width(32)) u_r3 (.D(Write_Data), .en(en3), .Q(r3), .clk(clk), .clr(clr));
  Register #(.width(32)) u_r4 (.D(Write_Data), .en(en4), .Q(r4), .clk(clk), .clr(clr));
  Register #(.width(32)) u_r5 (.D(Write_Data), .en(en5), .Q(r5), .clk(clk), .clr(clr));
  Register #(.width(32)) u_r6 (.D(Write_Data), .en(en6), .Q(r6), .clk(clk), .clr(clr));
  Register #(.width(32)) u_r7 (.D(Write_Data), .en(en7), .Q(r7), .clk(clk), .clr(clr));
  Multiplexer #(.select(3), .width(32), .enable("false")) multiplexer_1 (
    .in0({32{1'b0}}), .in1(r1), .in2(r2), .in3(r3), .in4(r4), .in5(r5), .in6(r6), .in7(r7), .out(Reg1_Data),
    .sel(Reg1__0_2));
  Multiplexer #(.select(3), .width(32), .enable("false")) multiplexer_2 (
    .in0({32{1'b0}}), .in1(r1), .in2(r2), .in3(r3), .in4(r4), .in5(r5), .in6(r6), .in7(r7), .out(Reg2_Data),
    .sel(Reg2__0_2));

  // Other names for the same wires on the sheet: WD[31:0] = Write_Data
endmodule

module _8_Reg (
  input  [31:0] Write_Data,
  input  [2:0] Reg1__0_2,
  input  clk,
  input  clr,
  input  [2:0] Wr_Reg__0_2,
  input  wen,
  input  [2:0] Reg2__0_2,
  output [31:0] Reg1_Data,
  output [31:0] Reg2_Data
);

  wire en0, en1, en2, en3, en4, en5, en6, en7;
  wire [31:0] r0, r1, r2, r3, r4, r5, r6, r7;

  Demultiplexer #(.select(3), .enable("false")) demultiplexer_1 (
    .out0(en0), .out1(en1), .out2(en2), .out3(en3), .out4(en4), .out5(en5), .out6(en6), .out7(en7), .in(wen),
    .sel(Wr_Reg__0_2));
  Register #(.width(32)) u_r0 (.D(Write_Data), .en(en0), .Q(r0), .clk(clk), .clr(clr));
  Register #(.width(32)) u_r1 (.D(Write_Data), .en(en1), .Q(r1), .clk(clk), .clr(clr));
  Register #(.width(32)) u_r2 (.D(Write_Data), .en(en2), .Q(r2), .clk(clk), .clr(clr));
  Register #(.width(32)) u_r3 (.D(Write_Data), .en(en3), .Q(r3), .clk(clk), .clr(clr));
  Register #(.width(32)) u_r4 (.D(Write_Data), .en(en4), .Q(r4), .clk(clk), .clr(clr));
  Register #(.width(32)) u_r5 (.D(Write_Data), .en(en5), .Q(r5), .clk(clk), .clr(clr));
  Register #(.width(32)) u_r6 (.D(Write_Data), .en(en6), .Q(r6), .clk(clk), .clr(clr));
  Register #(.width(32)) u_r7 (.D(Write_Data), .en(en7), .Q(r7), .clk(clk), .clr(clr));
  Multiplexer #(.select(3), .width(32), .enable("false")) multiplexer_1 (
    .in0(r0), .in1(r1), .in2(r2), .in3(r3), .in4(r4), .in5(r5), .in6(r6), .in7(r7), .out(Reg1_Data),
    .sel(Reg1__0_2));
  Multiplexer #(.select(3), .width(32), .enable("false")) multiplexer_2 (
    .in0(r0), .in1(r1), .in2(r2), .in3(r3), .in4(r4), .in5(r5), .in6(r6), .in7(r7), .out(Reg2_Data),
    .sel(Reg2__0_2));

  // Other names for the same wires on the sheet: WD[31:0] = Write_Data
endmodule

module Imm_Decoder (
  input  [24:0] Imm_Bits,
  input  [2:0] Imm_Encoding,
  output [31:0] Immediate
);

  wire [31:0] bit_extender_1_out, I, S, SB, U, UJ;

  assign bit_extender_1_out = {{12{Imm_Bits[24]}}, Imm_Bits[24:5]};  // Bit_Extender bit_extender_1
  assign I = {{20{Imm_Bits[24]}}, Imm_Bits[24:13]};  // Bit_Extender bit_extender_2
  assign S = {{20{Imm_Bits[24]}}, {Imm_Bits[24:18], Imm_Bits[4:0]}};  // Bit_Extender bit_extender_3
  assign SB = {{19{Imm_Bits[24]}}, {Imm_Bits[24], Imm_Bits[0], Imm_Bits[23:18], Imm_Bits[4:1], 1'b0}};  // Bit_Extender bit_extender_4
  Shifter #(.width(32)) shifter_1 (.in(bit_extender_1_out), .\dist (5'b01100), .out(U));
  assign UJ = {{11{Imm_Bits[24]}}, {Imm_Bits[24], Imm_Bits[12:5], Imm_Bits[13], Imm_Bits[23:14], 1'b0}};  // Bit_Extender bit_extender_5
  Multiplexer #(.select(3), .width(32), .disabled(0), .enable("false")) multiplexer_1 (
    .in0(I), .in1(S), .in2(SB), .in3(UJ), .in4(U), .in5(32'hbad), .in7(32'hbad), .out(Immediate),
    .sel(Imm_Encoding));  // open: in6

  // Other names for the same wires on the sheet: Enc[2:0] = Imm_Encoding
endmodule

module ALU (
  input  [31:0] In_1,
  input  [31:0] In_2,
  input  [3:0] Op,
  output [31:0] Out
);

  wire comparator_1_lt, comparator_2_lt;
  wire [31:0] add, \and , div, mul, mulh, \or , rem, sll, slt, sltu, sra, srl, sub, \xor ;

  Adder #(.width(32)) adder_1 (.a(In_1), .b(In_2), .out(add));  // open: cin, cout
  Subtractor #(.width(32)) subtractor_1 (.a(In_1), .b(In_2), .out(sub));  // open: bin, bout
  Multiplier #(.width(32)) multiplier_1 (.a(In_1), .b(In_2), .out(mul), .cout(mulh));  // open: cin
  Divider #(.width(32)) divider_1 (.a(In_1), .b(In_2), .out(div), .rem(rem));  // open: upper
  Shifter #(.width(32)) shifter_1 (.in(In_1), .\dist (In_2[4:0]), .out(sll));
  Shifter #(.width(32), .shift("lr")) shifter_2 (.in(In_1), .\dist (In_2[4:0]), .out(srl));
  Shifter #(.width(32), .shift("ar")) shifter_3 (.in(In_1), .\dist (In_2[4:0]), .out(sra));
  Comparator #(.width(32)) comparator_1 (.a(In_1), .b(In_2), .lt(comparator_1_lt));  // open: gt, eq
  Comparator #(.width(32), .mode("unsigned")) comparator_2 (.a(In_1), .b(In_2), .lt(comparator_2_lt));  // open: gt, eq
  assign \or  = In_1 | In_2;  // OR_Gate or_1, 32 bits wide
  assign \and  = In_1 & In_2;  // AND_Gate and_1, 32 bits wide
  assign \xor  = In_1 ^ In_2;  // XOR_Gate xor_1, 32 bits wide
  assign slt = {{31{1'b0}}, comparator_1_lt};  // Bit_Extender bit_extender_1
  assign sltu = {{31{1'b0}}, comparator_2_lt};  // Bit_Extender bit_extender_2
  Multiplexer #(.select(4), .width(32), .enable("false")) multiplexer_1 (
    .in0(add), .in1(sub), .in2(mul), .in3(mulh), .in4(div), .in5(rem), .in6(sll), .in7(srl), .in8(sra),
    .in9(slt), .in10(sltu), .in11(\or ), .in12(\and ), .in13(\xor ), .in14(In_2), .in15(32'hbad), .out(Out),
    .sel(Op));
endmodule

module Branch_Comp (
  input  [31:0] rs1,
  input  Unsign,
  input  [31:0] rs2,
  output Eq,
  output LT
);

  wire SEq, SLT, UEq, ULT;

  Comparator #(.width(32)) comparator_1 (.a(rs1), .b(rs2), .eq(SEq), .lt(SLT));  // open: gt
  Comparator #(.width(32), .mode("unsigned")) comparator_2 (.a(rs1), .b(rs2), .eq(UEq), .lt(ULT));  // open: gt
  Multiplexer #(.enable("false")) multiplexer_1 (.in0(SEq), .in1(UEq), .out(Eq), .sel(Unsign));
  Multiplexer #(.enable("false")) multiplexer_2 (.in0(SLT), .in1(ULT), .out(LT), .sel(Unsign));
endmodule

module Control (
  input  [31:0] Instr,
  input  LT,
  input  Eq,
  output Valid_Instr,
  output Continue_Execution,
  output [2:0] Imm_Enc,
  output BComp_U,
  output ALU_In_1,
  output ALU_In_2,
  output [3:0] ALU_Op,
  output RAM_WEn,
  output RAM_Read_U,
  output [1:0] WB_Sel,
  output Reg_WEn,
  output Next_PC_Sel
);

  wire multiplexer_1_out, Next_PC_Cond, Next_PC_Uncond, not_1_out, not_2_out;
  wire [1:0] BComp;

  // Probe on {Instr[6:0], Instr[14:12], Instr[30], Instr[25]}
  ROM #(.addrWidth(12), .dataWidth(21)) rom_1 (
    .addr({Instr[6:0], Instr[14:12], Instr[30], Instr[25]}),
    .data({Valid_Instr, Continue_Execution, Imm_Enc, BComp_U, BComp, Next_PC_Uncond, Next_PC_Cond, ALU_In_1, ALU_In_2, ALU_Op, RAM_WEn, RAM_Read_U, WB_Sel, Reg_WEn}));  // open: sel
  not not_1 (not_1_out, LT);
  not not_2 (not_2_out, Eq);
  Multiplexer #(.select(2), .enable("false")) multiplexer_1 (
    .in0(LT), .in1(not_1_out), .in2(Eq), .in3(not_2_out), .out(multiplexer_1_out), .sel(BComp));
  Multiplexer #(.enable("false")) multiplexer_2 (
    .in0(Next_PC_Uncond), .in1(multiplexer_1_out), .out(Next_PC_Sel), .sel(Next_PC_Cond));

  // Other names for the same wires on the sheet: Reg_Wr_En = Reg_WEn; RAM_Wr_En = RAM_WEn;
  //   Stop_Execution = Continue_Execution; Invalid_Instr = Valid_Instr

  // Notes on the sheet:
  //   Microcode
  //   contents of rom_1 (hex, n*v repeats v):
  //   96*180000 16*205 12*20d 484*180000 4*203 4*2c3 4*323 4*343 4*3a3 2e3 180000 303 180000 4*363 4*383
  //   96*180000 32*40203 352*180000 16*10210 496*180000 3 43 23 180000 c3 63 c3 63 4*123 4*143 1a3 83 1a3
  //   83 e3 e3 103 103 163 a3 163 a3 4*183 96*180000 32*403c3 1376*180000 4*24e00 4*26e00 8*180000 4*20e00
  //   4*22e00 4*28e00 4*2ae00 96*180000 4*1201 252*180000 32*31601 96*180000 32*80000 384*180000
endmodule

module RAM (
  input  [31:0] ALU,
  input  [31:0] Write_Data,
  input  clk,
  input  clr,
  input  Wr_En,
  input  [2:0] Funct3,
  input  Read_Unsigned,
  output [31:0] RAM_Out
);

  wire [7:0] b0_out, b1_out, b2_out, b3_out;
  wire [22:0] H110;
  wire [31:0] extend_byte_s_1_out, extend_byte_s_2_out, extend_byte_s_3_out, extend_byte_s_4_out,
       extend_byte_u_1_out, extend_byte_u_2_out, extend_byte_u_3_out, extend_byte_u_4_out,
       extend_half_s_1_out, extend_half_s_2_out, extend_half_s_3_out, extend_half_s_4_out,
       extend_half_u_1_out, extend_half_u_2_out, extend_half_u_3_out, extend_half_u_4_out,
       extend_tronple_s_1_out, extend_tronple_s_2_out, extend_tronple_s_3_out, extend_tronple_s_4_out,
       extend_tronple_u_1_out, extend_tronple_u_2_out, extend_tronple_u_3_out, extend_tronple_u_4_out,
       multiplexer_1_out, multiplexer_2_out, multiplexer_3_out, multiplexer_4_out;

  Adder #(.width(23)) adder_1 (.a(ALU[24:2]), .b(23'h1), .out(H110));  // open: cin, cout
  Multiplexer #(.select(4), .width(32), .enable("false")) multiplexer_1 (
    .in0({Wr_En, Write_Data[7:0], ALU[24:2]}), .in1({32{1'b0}}), .in2({32{1'b0}}), .in3({32{1'b0}}),
    .in4({Wr_En, Write_Data[7:0], ALU[24:2]}), .in5({32{1'b0}}), .in6({32{1'b0}}),
    .in7({Wr_En, Write_Data[15:8], H110}), .in8({Wr_En, Write_Data[7:0], ALU[24:2]}), .in9({32{1'b0}}),
    .in10({Wr_En, Write_Data[23:16], H110}), .in11({Wr_En, Write_Data[15:8], H110}),
    .in12({Wr_En, Write_Data[7:0], ALU[24:2]}), .in13({Wr_En, Write_Data[31:24], H110}),
    .in14({Wr_En, Write_Data[23:16], H110}), .in15({Wr_En, Write_Data[15:8], H110}), .out(multiplexer_1_out),
    .sel({Funct3[1:0], ALU[1:0]}));
  Multiplexer #(.select(4), .width(32), .enable("false")) multiplexer_2 (
    .in0({32{1'b0}}), .in1({Wr_En, Write_Data[7:0], ALU[24:2]}), .in2({32{1'b0}}), .in3({32{1'b0}}),
    .in4({Wr_En, Write_Data[15:8], ALU[24:2]}), .in5({Wr_En, Write_Data[7:0], ALU[24:2]}), .in6({32{1'b0}}),
    .in7({32{1'b0}}), .in8({Wr_En, Write_Data[15:8], ALU[24:2]}), .in9({Wr_En, Write_Data[7:0], ALU[24:2]}),
    .in10({32{1'b0}}), .in11({Wr_En, Write_Data[23:16], H110}), .in12({Wr_En, Write_Data[15:8], ALU[24:2]}),
    .in13({Wr_En, Write_Data[7:0], ALU[24:2]}), .in14({Wr_En, Write_Data[31:24], H110}),
    .in15({Wr_En, Write_Data[23:16], H110}), .out(multiplexer_2_out), .sel({Funct3[1:0], ALU[1:0]}));
  Multiplexer #(.select(4), .width(32), .enable("false")) multiplexer_3 (
    .in0({32{1'b0}}), .in1({32{1'b0}}), .in2({Wr_En, Write_Data[7:0], ALU[24:2]}), .in3({32{1'b0}}),
    .in4({32{1'b0}}), .in5({Wr_En, Write_Data[15:8], ALU[24:2]}), .in6({Wr_En, Write_Data[7:0], ALU[24:2]}),
    .in7({32{1'b0}}), .in8({Wr_En, Write_Data[23:16], ALU[24:2]}),
    .in9({Wr_En, Write_Data[15:8], ALU[24:2]}), .in10({Wr_En, Write_Data[7:0], ALU[24:2]}),
    .in11({32{1'b0}}), .in12({Wr_En, Write_Data[23:16], ALU[24:2]}),
    .in13({Wr_En, Write_Data[15:8], ALU[24:2]}), .in14({Wr_En, Write_Data[7:0], ALU[24:2]}),
    .in15({Wr_En, Write_Data[31:24], H110}), .out(multiplexer_3_out), .sel({Funct3[1:0], ALU[1:0]}));
  Multiplexer #(.select(4), .width(32), .enable("false")) multiplexer_4 (
    .in0({32{1'b0}}), .in1({32{1'b0}}), .in2({32{1'b0}}), .in3({Wr_En, Write_Data[7:0], ALU[24:2]}),
    .in4({32{1'b0}}), .in5({32{1'b0}}), .in6({Wr_En, Write_Data[15:8], ALU[24:2]}),
    .in7({Wr_En, Write_Data[7:0], ALU[24:2]}), .in8({32{1'b0}}), .in9({Wr_En, Write_Data[23:16], ALU[24:2]}),
    .in10({Wr_En, Write_Data[15:8], ALU[24:2]}), .in11({Wr_En, Write_Data[7:0], ALU[24:2]}),
    .in12({Wr_En, Write_Data[31:24], ALU[24:2]}), .in13({Wr_En, Write_Data[23:16], ALU[24:2]}),
    .in14({Wr_En, Write_Data[15:8], ALU[24:2]}), .in15({Wr_En, Write_Data[7:0], ALU[24:2]}),
    .out(multiplexer_4_out), .sel({Funct3[1:0], ALU[1:0]}));
  RAM_part #(.addrWidth(23), .bus("separate")) ram_1 (
    .addr(multiplexer_1_out[22:0]), .din(multiplexer_1_out[30:23]), .data(b0_out),
    .str(multiplexer_1_out[31]), .clk(clk), .clr(clr));  // open: sel, ld
  RAM_part #(.addrWidth(23), .bus("separate")) ram_2 (
    .addr(multiplexer_2_out[22:0]), .din(multiplexer_2_out[30:23]), .data(b1_out),
    .str(multiplexer_2_out[31]), .clk(clk), .clr(clr));  // open: sel, ld
  RAM_part #(.addrWidth(23), .bus("separate")) ram_3 (
    .addr(multiplexer_3_out[22:0]), .din(multiplexer_3_out[30:23]), .data(b2_out),
    .str(multiplexer_3_out[31]), .clk(clk), .clr(clr));  // open: sel, ld
  RAM_part #(.addrWidth(23), .bus("separate")) ram_4 (
    .addr(multiplexer_4_out[22:0]), .din(multiplexer_4_out[30:23]), .data(b3_out),
    .str(multiplexer_4_out[31]), .clk(clk), .clr(clr));  // open: sel, ld
  Extend_Byte_S extend_byte_s_1 (.In(b0_out), .Out(extend_byte_s_1_out));
  Extend_Byte_U extend_byte_u_1 (.In(b0_out), .Out(extend_byte_u_1_out));
  Extend_Byte_S extend_byte_s_2 (.In(b1_out), .Out(extend_byte_s_2_out));
  Extend_Byte_U extend_byte_u_2 (.In(b1_out), .Out(extend_byte_u_2_out));
  Extend_Byte_S extend_byte_s_3 (.In(b2_out), .Out(extend_byte_s_3_out));
  Extend_Byte_U extend_byte_u_3 (.In(b2_out), .Out(extend_byte_u_3_out));
  Extend_Byte_S extend_byte_s_4 (.In(b3_out), .Out(extend_byte_s_4_out));
  Extend_Byte_U extend_byte_u_4 (.In(b3_out), .Out(extend_byte_u_4_out));
  Extend_Half_S extend_half_s_1 (.In({b1_out, b0_out}), .Out(extend_half_s_1_out));
  Extend_Half_U extend_half_u_1 (.In({b1_out, b0_out}), .Out(extend_half_u_1_out));
  Extend_Half_S extend_half_s_2 (.In({b2_out, b1_out}), .Out(extend_half_s_2_out));
  Extend_Half_U extend_half_u_2 (.In({b2_out, b1_out}), .Out(extend_half_u_2_out));
  Extend_Half_S extend_half_s_3 (.In({b3_out, b2_out}), .Out(extend_half_s_3_out));
  Extend_Half_U extend_half_u_3 (.In({b3_out, b2_out}), .Out(extend_half_u_3_out));
  Extend_Half_S extend_half_s_4 (.In({b0_out, b3_out}), .Out(extend_half_s_4_out));
  Extend_Half_U extend_half_u_4 (.In({b0_out, b3_out}), .Out(extend_half_u_4_out));
  Extend_Tronple_S extend_tronple_s_1 (.In({b2_out, b1_out, b0_out}), .Out(extend_tronple_s_1_out));
  Extend_Tronple_U extend_tronple_u_1 (.In({b2_out, b1_out, b0_out}), .Out(extend_tronple_u_1_out));
  Extend_Tronple_S extend_tronple_s_2 (.In({b3_out, b2_out, b1_out}), .Out(extend_tronple_s_2_out));
  Extend_Tronple_U extend_tronple_u_2 (.In({b3_out, b2_out, b1_out}), .Out(extend_tronple_u_2_out));
  Extend_Tronple_S extend_tronple_s_3 (.In({b0_out, b3_out, b2_out}), .Out(extend_tronple_s_3_out));
  Extend_Tronple_U extend_tronple_u_3 (.In({b0_out, b3_out, b2_out}), .Out(extend_tronple_u_3_out));
  Extend_Tronple_S extend_tronple_s_4 (.In({b1_out, b0_out, b3_out}), .Out(extend_tronple_s_4_out));
  Extend_Tronple_U extend_tronple_u_4 (.In({b1_out, b0_out, b3_out}), .Out(extend_tronple_u_4_out));
  Multiplexer #(.select(5), .width(32), .enable("false")) multiplexer_5 (
    .in0(extend_byte_s_1_out), .in1(extend_byte_u_1_out), .in2(extend_byte_s_2_out),
    .in3(extend_byte_u_2_out), .in4(extend_byte_s_3_out), .in5(extend_byte_u_3_out),
    .in6(extend_byte_s_4_out), .in7(extend_byte_u_4_out), .in8(extend_half_s_1_out),
    .in9(extend_half_u_1_out), .in10(extend_half_s_2_out), .in11(extend_half_u_2_out),
    .in12(extend_half_s_3_out), .in13(extend_half_u_3_out), .in14(extend_half_s_4_out),
    .in15(extend_half_u_4_out), .in16(extend_tronple_s_1_out), .in17(extend_tronple_u_1_out),
    .in18(extend_tronple_s_2_out), .in19(extend_tronple_u_2_out), .in20(extend_tronple_s_3_out),
    .in21(extend_tronple_u_3_out), .in22(extend_tronple_s_4_out), .in23(extend_tronple_u_4_out),
    .in24({b3_out, b2_out, b1_out, b0_out}), .in25({b3_out, b2_out, b1_out, b0_out}),
    .in26({b0_out, b3_out, b2_out, b1_out}), .in27({b0_out, b3_out, b2_out, b1_out}),
    .in28({b1_out, b0_out, b3_out, b2_out}), .in29({b1_out, b0_out, b3_out, b2_out}),
    .in30({b2_out, b1_out, b0_out, b3_out}), .in31({b2_out, b1_out, b0_out, b3_out}), .out(RAM_Out),
    .sel({Funct3[1:0], ALU[1:0], Read_Unsigned}));

  // Other names for the same wires on the sheet: Byte_Index[1:0] = ALU[1:0]; Encoding[3:0] = {Funct3[1:0], ALU[1:0]};
  //   RAM_num[1:0] = Funct3[1:0]; b1[7:0] = Write_Data[15:8]; H001[31:0] = {Wr_En, Write_Data[15:8], ALU[24:2]};
  //   H012[31:0] = {Wr_En, Write_Data[15:8], ALU[24:2]}; H103[31:0] = {Wr_En, Write_Data[15:8], ALU[24:2]};
  //   H110[31:23] = {Wr_En, Write_Data[15:8]}; T001[31:0] = {Wr_En, Write_Data[15:8], ALU[24:2]};
  //   T012[31:0] = {Wr_En, Write_Data[15:8], ALU[24:2]}; T103[31:0] = {Wr_En, Write_Data[15:8], ALU[24:2]};
  //   T110[31:0] = {Wr_En, Write_Data[15:8], H110}; W001[31:0] = {Wr_En, Write_Data[15:8], ALU[24:2]};
  //   W012[31:0] = {Wr_En, Write_Data[15:8], ALU[24:2]}; W103[31:0] = {Wr_En, Write_Data[15:8], ALU[24:2]};
  //   W110[31:0] = {Wr_En, Write_Data[15:8], H110}; b2[7:0] = Write_Data[23:16];
  //   T002[31:0] = {Wr_En, Write_Data[23:16], ALU[24:2]}; T013[31:0] = {Wr_En, Write_Data[23:16], ALU[24:2]};
  //   T100[31:0] = {Wr_En, Write_Data[23:16], H110}; T111[31:0] = {Wr_En, Write_Data[23:16], H110};
  //   W002[31:0] = {Wr_En, Write_Data[23:16], ALU[24:2]}; W013[31:0] = {Wr_En, Write_Data[23:16], ALU[24:2]};
  //   W100[31:0] = {Wr_En, Write_Data[23:16], H110}; W111[31:0] = {Wr_En, Write_Data[23:16], H110};
  //   W010[31:0] = {Wr_En, Write_Data[31:24], H110}; W101[31:0] = {Wr_En, Write_Data[31:24], H110};
  //   W112[31:0] = {Wr_En, Write_Data[31:24], H110}; Word_Align___1[22:0] = H110; b3[7:0] = Write_Data[31:24];
  //   W003[31:0] = {Wr_En, Write_Data[31:24], ALU[24:2]}; B000[31:0] = {Wr_En, Write_Data[7:0], ALU[24:2]};
  //   B011[31:0] = {Wr_En, Write_Data[7:0], ALU[24:2]}; B102[31:0] = {Wr_En, Write_Data[7:0], ALU[24:2]};
  //   B113[31:0] = {Wr_En, Write_Data[7:0], ALU[24:2]}; H000[31:0] = {Wr_En, Write_Data[7:0], ALU[24:2]};
  //   H011[31:0] = {Wr_En, Write_Data[7:0], ALU[24:2]}; H102[31:0] = {Wr_En, Write_Data[7:0], ALU[24:2]};
  //   H113[31:0] = {Wr_En, Write_Data[7:0], ALU[24:2]}; T000[31:0] = {Wr_En, Write_Data[7:0], ALU[24:2]};
  //   T011[31:0] = {Wr_En, Write_Data[7:0], ALU[24:2]}; T102[31:0] = {Wr_En, Write_Data[7:0], ALU[24:2]};
  //   T113[31:0] = {Wr_En, Write_Data[7:0], ALU[24:2]}; W000[31:0] = {Wr_En, Write_Data[7:0], ALU[24:2]};
  //   W011[31:0] = {Wr_En, Write_Data[7:0], ALU[24:2]}; W102[31:0] = {Wr_En, Write_Data[7:0], ALU[24:2]};
  //   W113[31:0] = {Wr_En, Write_Data[7:0], ALU[24:2]}; Word_Align[22:0] = ALU[24:2]; b0[7:0] = Write_Data[7:0];
  //   wen = Wr_En

  // Notes on the sheet:
  //    (00) Byte
  //   (01) Half
  //   (10) Tronple
  //   (11) Word
  //   0
  //   1
  //   2
  //   3
  //   0
  //   1
  //   2
  //   3
  //   0
  //   1
  //   2
  //   3
  //   0
  //   1
  //   2
  //   3
  //   00
  //   0
  //   1
  //   2
  //   3
  //   0
  //   1
  //   2
  //   3
  //   0
  //   1
  //   2
  //   3
  //   0
  //   1
  //   2
  //   3
  //   01
  //   Encoding = RAM# | Byte Index
  //   0
  //   1
  //   2
  //   3
  //   0
  //   1
  //   2
  //   3
  //   0
  //   1
  //   2
  //   3
  //   0
  //   1
  //   2
  //   3
  //   10
  //   0
  //   1
  //   2
  //   3
  //   0
  //   1
  //   2
  //   3
  //   0
  //   1
  //   2
  //   3
  //   0
  //   1
  //   2
  //   3
  //   11
  //   Byte 0
  //   Byte 1
  //   Byte 2
  //   Byte 3
endmodule

module Extend_Byte_S (
  input  [7:0] In,
  output [31:0] Out
);

  assign Out = {{24{In[7]}}, In};  // Bit_Extender bit_extender_1
endmodule

module Extend_Byte_U (
  input  [7:0] In,
  output [31:0] Out
);

  assign Out = {{24{1'b0}}, In};  // Bit_Extender bit_extender_1
endmodule

module Extend_Half_S (
  input  [15:0] In,
  output [31:0] Out
);

  assign Out = {{16{In[15]}}, In};  // Bit_Extender bit_extender_1
endmodule

module Extend_Half_U (
  input  [15:0] In,
  output [31:0] Out
);

  assign Out = {{16{1'b0}}, In};  // Bit_Extender bit_extender_1
endmodule

module Extend_Tronple_S (
  input  [23:0] In,
  output [31:0] Out
);

  assign Out = {{8{In[23]}}, In};  // Bit_Extender bit_extender_1
endmodule

module Extend_Tronple_U (
  input  [23:0] In,
  output [31:0] Out
);

  assign Out = {{8{1'b0}}, In};  // Bit_Extender bit_extender_1
endmodule
